# Fritzing sketch MZE2_FrontPanel Circuit (saved by Fritzing 0.9.2b)
breadboards: 1

parts:
  LED1 = LED - 5mm [color="Red (633nm)" package="5 mm [THT]"]
  R1 = Resistor [tolerance=±5% resistance=1k package=THT]
  Q2 = PNP-Transistor [package="SOT-23 [SMD]"]
  R2 = Resistor [tolerance=±5% resistance=470 package=THT]
  LED2 = LED - 5mm [color="Green (555nm)" package="5 mm [THT]"]
  R3 = Resistor [tolerance=±5% resistance=1k package=THT]
  J2 = shrouded pin header, 12 pins [form="♂ (shrouded male)"]
  R4 = Resistor [tolerance=±5% resistance=4.7k package=THT]
  R5 = Resistor [tolerance=±5% resistance=4.7 package=THT]
  IC2 = DIP - 14 pins [chip_label=74HC164D package="DIP (Dual Inline) [THT]"]
  R6 = Resistor [tolerance=±5% resistance=1k package=THT]
  R7 = Resistor [tolerance=±5% resistance=330 package=THT]
  Q4 = PNP-Transistor [package="TO92 [THT]"]
  Q3 = PNP-Transistor [package="SOT-23 [SMD]"]
  Q5 = PNP-Transistor [package="SOT-23 [SMD]"]
  R8 = Resistor [tolerance=±5% resistance=1k package=THT]
  R9 = Resistor [tolerance=±5% resistance=330 package=THT]
  Q6 = PNP-Transistor [package="SOT-23 [SMD]"]
  R10 = Resistor [tolerance=±5% resistance=1k package=THT]
  R11 = Resistor [tolerance=±5% resistance=330 package=THT]
  Q7 = PNP-Transistor [package="SOT-23 [SMD]"]
  R12 = Resistor [tolerance=±5% resistance=1k package=THT]
  R13 = Resistor [tolerance=±5% resistance=330 package=THT]
  IC3 = IC, DIP package, 16 pins [chip_label=4x7segments]
  R14 = Resistor [tolerance=±5% resistance=33 package=THT]
  R15 = Resistor [tolerance=±5% resistance=33 package=THT]
  R16 = Resistor [tolerance=±5% resistance=33 package=THT]
  R17 = Resistor [tolerance=±5% resistance=33 package=THT]
  R18 = Resistor [tolerance=±5% resistance=33 package=THT]
  R19 = Resistor [tolerance=±5% resistance=33 package=THT]
  R20 = Resistor [tolerance=±5% resistance=33 package=THT]
  R21 = Resistor [tolerance=±5% resistance=33 package=THT]
  S1 = Pushbutton [part_number="SW6 - Menu - Q4" package="[THT]"]
  S2 = Pushbutton [part_number="SW5 - ok - Q5" package="[THT]"]
  S3 = Pushbutton [part_number="SW2 - CH- - Q1" package="[THT]"]
  S4 = Pushbutton [part_number="SW4 - VOL+ - Q3" package="[THT]"]
  S5 = Pushbutton [part_number="SW3 - VOL- - Q2" package="[THT]"]
  S6 = Pushbutton [part_number="SW1 - CH+ - Q0" package="[THT]"]
  S7 = Pushbutton [part_number="SW7 - POWER - Q6" package="[THT]"]
  R22 = Resistor [tolerance=±5% resistance=4.68k package=THT]
  IR1 = TSOP312.., 314.. [package=THT]
  R23 = Resistor [tolerance=±5% resistance=18 package=THT]
  R24 = Resistor [tolerance=±5% resistance=4.68k package=THT]
  C1 = Electrolytic Capacitor [capacitance=1µF package="100 mil [THT, electrolytic]"]

nets:
  N1: LED1.cathode, R1.Pin_0
  1: LED1.anode, LED2.anode, R4.Pin_1, R5.Pin_0, IC2.MR, IC2.Vcc, R7.Pin_1, Q3.2, Q5.2, R9.Pin_1, Q6.2, R11.Pin_1, Q7.2, R13.Pin_1, R22.Pin_1, R23.Pin_0, R24.Pin_1
  3/GND: R1.Pin_1, Q2.1, J2.pin3, J2.pin8, IC2.GND
  N2: Q2.2, R2.Pin_1
  N3: Q2.0, R3.Pin_1
  N4: R2.Pin_0, LED2.cathode
  4: R3.Pin_0
  5V: J2.pin1
  LED verte: J2.pin4
  Serial In: J2.pin5
  CP: J2.pin6
  buttons: J2.pin7
  Digit 4: J2.pin9
  Digit 3: J2.pin10
  Digit 2: J2.pin11
  Digit 1: J2.pin12
  5: R4.Pin_0, IC2.DSA, IC2.DSB
  6: R5.Pin_1, IC2.CP
  N5: IC2.Q0, R17.Pin_0
  N6: IC2.Q1, R18.Pin_0
  N7: IC2.Q2, R19.Pin_1
  N8: IC2.Q3, R20.Pin_1
  N9: IC2.Q4, R16.Pin_1
  N10: IC2.Q5, R15.Pin_0
  N11: IC2.Q6, R14.Pin_0
  N12: IC2.Q7, R21.Pin_0
  12: R6.Pin_0
  N13: R6.Pin_1, R7.Pin_0, Q3.0
  E: Q4.E
  B: Q4.B
  C: Q4.C
  N14: Q3.1, IC3.pin1
  N15: Q5.0, R8.Pin_1, R9.Pin_0
  N16: Q5.1, IC3.pin2
  11: R8.Pin_0
  N17: Q6.0, R10.Pin_1, R11.Pin_0
  N18: Q6.1, IC3.pin4, IC3.pin6
  10: R10.Pin_0
  N19: Q7.0, R12.Pin_1, R13.Pin_0
  N20: Q7.1, IC3.pin8
  9: R12.Pin_0
  N21: IC3.pin3, R20.Pin_0, S4.Pin_3, S4.Pin_4
  N22: IC3.pin5, R16.Pin_0, S1.Pin_1, S1.Pin_2
  N23: IC3.pin11, R15.Pin_1, S2.Pin_1
  N24: IC3.pin12, R21.Pin_1
  N25: IC3.pin13, R19.Pin_0, S5.Pin_3, S5.Pin_4
  N26: IC3.pin14, R17.Pin_1, S6.Pin_3, S6.Pin_4
  N27: IC3.pin15, R14.Pin_1, S7.Pin_1
  N28: IC3.pin16, R18.Pin_1, S3.Pin_3, S3.Pin_4
  7: S1.Pin_3, S1.Pin_4, S2.Pin_3, S2.Pin_4, S3.Pin_1, S4.Pin_1, S4.Pin_2, S5.Pin_1, S6.Pin_1, S7.Pin_3, R22.Pin_0
  N29: IR1.GND, C1.-
  N30: IR1.Vs, R23.Pin_1, C1.+
  2: IR1.Data, R24.Pin_0

notes:
  pin4 - LOW -> light up LED

custom parts:
  DIP - 14 pins: A DIP stand-in part for whatever IC you want. With 14 pins on a 300mil dual inline package (DIP) footprint.
